// Logisim project PBP1204.circ as structural Verilog: 1 circuit, main circuit main
module main (
);

  wire CLK, RESET, RW;
  wire [0:0] ledbar_3_p1;
  wire [3:0] DATA, InstructionCounter_q, InstructionRegister_q;
  wire [7:0] Microcode_data;
  wire [11:0] ADDRESS;

  // LedBar #(.inputtype("row"), .matrixcols(12)) ledbar_1: pin names not known; wires that end beside it: ADDRESS
  // LedBar #(.inputtype("row"), .matrixcols(4)) ledbar_2: pin names not known; wires that end beside it: DATA
  Counter #(.max('hf), .width(4)) InstructionCounter (.Q(InstructionCounter_q));  // open: clr, load, up, count, clk, D, carry
  // LedBar #(.inputtype("row"), .matrixcols(4)) ledbar_3: pin names not known; wires that end beside it: {RW, RESET, CLK, ledbar_3_p1[0]}
  Register #(.width(4)) InstructionRegister (.Q(InstructionRegister_q));  // open: D, en, clk, clr
  ROM Microcode (.addr({InstructionRegister_q, InstructionCounter_q}), .data(Microcode_data));
  D_Flip_Flop CarryFlag ();  // open: D, clk, Q, Qn, preset, reset
  D_Flip_Flop ParityFlag ();  // open: D, clk, Q, Qn, preset, reset
  D_Flip_Flop BorrowFlag ();  // open: D, clk, Q, Qn, preset, reset
  Register #(.width(4)) ARegister ();  // open: D, en, clk, Q, clr
  Register #(.width(4)) BRegister ();  // open: D, en, clk, Q, clr
  Register #(.trigger("falling"), .width(4)) LowBuffer ();  // open: D, en, clk, Q, clr
  Register #(.width(4)) MidBuffer ();  // open: D, en, clk, Q, clr
  Register #(.width(4)) HiBuffer ();  // open: D, en, clk, Q, clr
  Counter #(.max('hfff), .width(12)) ProgramCounter ();  // open: clr, load, up, count, clk, D, carry, Q
  Counter #(.max('hfff), .width(12)) StackPointer ();  // open: clr, load, up, count, clk, D, carry, Q
  Register #(.width(12)) AddressBuffer ();  // open: D, en, clk, Q, clr
endmodule
